# Fritzing sketch Temperature Sensor (saved by Fritzing 0.9.3b)
breadboards: 1

parts:
  RHT1 = Humidity and Temperature Sensor RHT03
  WeMos_D1_Mini1 = WeMos D1 Mini

nets:
  VCC: RHT1.Vcc, WeMos_D1_Mini1.3V3
  N1: RHT1.Data-signal, WeMos_D1_Mini1.D1
  N2: RHT1.GND_1, WeMos_D1_Mini1.G
  N3: WeMos_D1_Mini1.D0, WeMos_D1_Mini1.RST
